// Logisim project aiALU.circ as structural Verilog
module SuperCircuit (
  input  [7:0] A,
  input  [7:0] B,
  input  Sel2,
  input  Cin,
  input  Sel1,
  input  Sel0,
  output [7:0] out_7,
  output out_8
);

  // Probe on A
  aiALU aialu_1 (.in_3(Cin), .in_4(Sel0), .in_1(A), .in_2(B), .out_6(out_7), .out_5(out_8));
  // Probe on B
  // Probe on out_7
endmodule

module aiALU (
  input  [7:0] in_1,
  input  [7:0] in_2,
  input  in_3,
  input  in_4,
  output out_5,
  output [7:0] out_6
);

  // Probe on in_1
  aiArith aiarith_1 (.A(in_1), .B(in_2), .in_3(in_3), .in_4(in_4), .out_6(out_6), .out_5(out_5));
  // Probe on in_2
  // Probe on out_6
endmodule

module aiArith (
  input  [7:0] A,
  input  [7:0] B,
  input  in_3,
  input  in_4,
  output out_5,
  output [7:0] out_6
);

  wire [7:0] and_1_out, and_2_out, bit_extender_1_out, bit_extender_2_out, n8bit_adder_1_out_27,
       n8bit_subtractor_1_out_5, not_1_out;

  _8bit_Adder u_8bit_adder_1 (
    .in_17(B[0]), .in_18(A[0]), .in_16(B[1]), .in_15(A[1]), .in_14(B[2]), .in_13(A[2]), .in_12(B[3]),
    .in_11(A[3]), .in_10(B[4]), .in_9(A[4]), .in_8(B[5]), .in_7(A[5]), .in_6(B[6]), .in_5(A[6]), .in_4(B[7]),
    .in_3(A[7]), .out_19(out_5), .out_20(n8bit_adder_1_out_27[7]), .out_21(n8bit_adder_1_out_27[6]),
    .out_22(n8bit_adder_1_out_27[5]), .out_23(n8bit_adder_1_out_27[4]), .out_24(n8bit_adder_1_out_27[3]),
    .out_25(n8bit_adder_1_out_27[2]), .out_26(n8bit_adder_1_out_27[1]), .out_27(n8bit_adder_1_out_27[0]),
    .in_1(in_4), .in_2(in_3));
  assign bit_extender_1_out = {{7{in_4}}, in_4};  // Bit_Extender bit_extender_1
  assign not_1_out = ~bit_extender_1_out;  // NOT_Gate not_1, 8 bits wide
  assign and_1_out = n8bit_adder_1_out_27 & not_1_out;  // AND_Gate and_1, 8 bits wide
  assign bit_extender_2_out = {{7{in_4}}, in_4};  // Bit_Extender bit_extender_2
  assign out_6 = and_1_out | and_2_out;  // OR_Gate or_1, 8 bits wide
  _8bit_Subtractor u_8bit_subtractor_1 (.in_1(A), .in_2(B), .out_5(n8bit_subtractor_1_out_5), .in_3(in_3), .in_4(in_4));
  assign and_2_out = bit_extender_2_out & n8bit_subtractor_1_out_5;  // AND_Gate and_2, 8 bits wide
endmodule

module HalfAdder (
  input  A,
  input  B,
  output S,
  output C
);

  xor xor_1 (S, A, B);
  and and_1 (C, A, B);
endmodule

module FullAdder (
  input  A,
  input  B,
  input  Cin,
  output Cout,
  output S
);

  wire halfadder_1_c, halfadder_2_c, halfadder_2_s;

  or or_1 (Cout, halfadder_2_c, halfadder_1_c);
  HalfAdder halfadder_1 (.A(halfadder_2_s), .B(Cin), .S(S), .C(halfadder_1_c));
  HalfAdder halfadder_2 (.A(A), .B(B), .S(halfadder_2_s), .C(halfadder_2_c));
endmodule

module _8bit_Adder (
  input  in_1,
  input  in_2,
  input  in_3,
  input  in_4,
  input  in_5,
  input  in_6,
  input  in_7,
  input  in_8,
  input  in_9,
  input  in_10,
  input  in_11,
  input  in_12,
  input  in_13,
  input  in_14,
  input  in_15,
  input  in_16,
  input  in_17,
  input  in_18,
  output out_19,
  output out_20,
  output out_21,
  output out_22,
  output out_23,
  output out_24,
  output out_25,
  output out_26,
  output out_27
);

  wire fulladder_2_cout, fulladder_3_cout, fulladder_4_cout, fulladder_5_cout, fulladder_6_cout,
       fulladder_7_cout, fulladder_8_cout, fulladder_9_cout, fulladder_9_s, or_1_out;

  FullAdder fulladder_1 (.A(in_4), .B(in_3), .Cin(fulladder_2_cout), .S(out_20), .Cout(out_19));
  FullAdder fulladder_2 (.A(in_6), .B(in_5), .Cin(fulladder_3_cout), .S(out_21), .Cout(fulladder_2_cout));
  FullAdder fulladder_3 (.A(in_8), .B(in_7), .Cin(fulladder_4_cout), .S(out_22), .Cout(fulladder_3_cout));
  FullAdder fulladder_4 (.A(in_10), .B(in_9), .Cin(fulladder_5_cout), .S(out_23), .Cout(fulladder_4_cout));
  FullAdder fulladder_5 (.A(in_12), .B(in_11), .Cin(fulladder_6_cout), .S(out_24), .Cout(fulladder_5_cout));
  FullAdder fulladder_6 (.A(in_14), .B(in_13), .Cin(fulladder_7_cout), .S(out_25), .Cout(fulladder_6_cout));
  FullAdder fulladder_7 (.A(in_16), .B(in_15), .Cin(fulladder_8_cout), .S(out_26), .Cout(fulladder_7_cout));
  FullAdder fulladder_8 (.A(in_18), .B(in_17), .Cin(or_1_out), .S(out_27), .Cout(fulladder_8_cout));
  FullAdder fulladder_9 (.A(in_2), .B(in_1), .Cin(1'b0), .S(fulladder_9_s), .Cout(fulladder_9_cout));
  or or_1 (or_1_out, fulladder_9_cout, fulladder_9_s);
endmodule

module _8bit_Subtractor (
  input  [7:0] in_1,
  input  [7:0] in_2,
  input  in_3,
  input  in_4,
  output [7:0] out_5
);

  wire [7:0] not_1_out;

  _8bit_Adder2 u_8bit_adder2_1 (
    .in_2(in_1[7]), .in_3(not_1_out[7]), .in_4(in_1[6]), .in_5(not_1_out[6]), .in_6(in_1[5]),
    .in_7(not_1_out[5]), .in_8(in_1[4]), .in_9(not_1_out[4]), .in_10(in_1[3]), .in_11(not_1_out[3]),
    .in_12(in_1[2]), .in_13(not_1_out[2]), .in_14(in_1[1]), .in_15(not_1_out[1]), .in_16(in_1[0]),
    .in_17(not_1_out[0]), .in_1(in_4), .out_20(out_5[7]), .out_21(out_5[6]), .out_22(out_5[5]),
    .out_23(out_5[4]), .out_24(out_5[3]), .out_25(out_5[2]), .out_26(out_5[1]), .out_27(out_5[0]),
    .in_18(in_3));  // open: out_19
  assign not_1_out = ~in_2;  // NOT_Gate not_1, 8 bits wide
endmodule

module _8bit_Adder2 (
  input  in_1,
  input  in_2,
  input  in_3,
  input  in_4,
  input  in_5,
  input  in_6,
  input  in_7,
  input  in_8,
  input  in_9,
  input  in_10,
  input  in_11,
  input  in_12,
  input  in_13,
  input  in_14,
  input  in_15,
  input  in_16,
  input  in_17,
  input  in_18,
  output out_19,
  output out_20,
  output out_21,
  output out_22,
  output out_23,
  output out_24,
  output out_25,
  output out_26,
  output out_27
);

  wire fulladder_2_cout, fulladder_3_cout, fulladder_4_cout, fulladder_5_cout, fulladder_6_cout,
       fulladder_7_cout, fulladder_8_cout, fulladder_9_cout, fulladder_9_s, or_1_out;

  FullAdder fulladder_1 (.A(in_3), .B(in_2), .Cin(fulladder_2_cout), .S(out_20), .Cout(out_19));
  FullAdder fulladder_2 (.A(in_5), .B(in_4), .Cin(fulladder_3_cout), .S(out_21), .Cout(fulladder_2_cout));
  FullAdder fulladder_3 (.A(in_7), .B(in_6), .Cin(fulladder_4_cout), .S(out_22), .Cout(fulladder_3_cout));
  FullAdder fulladder_4 (.A(in_9), .B(in_8), .Cin(fulladder_5_cout), .S(out_23), .Cout(fulladder_4_cout));
  FullAdder fulladder_5 (.A(in_11), .B(in_10), .Cin(fulladder_6_cout), .S(out_24), .Cout(fulladder_5_cout));
  FullAdder fulladder_6 (.A(in_13), .B(in_12), .Cin(fulladder_7_cout), .S(out_25), .Cout(fulladder_6_cout));
  FullAdder fulladder_7 (.A(in_15), .B(in_14), .Cin(fulladder_8_cout), .S(out_26), .Cout(fulladder_7_cout));
  FullAdder fulladder_8 (.A(in_17), .B(in_16), .Cin(or_1_out), .S(out_27), .Cout(fulladder_8_cout));
  FullAdder fulladder_9 (.A(in_1), .B(1'b0), .Cin(in_18), .S(fulladder_9_s), .Cout(fulladder_9_cout));
  or or_1 (or_1_out, fulladder_9_cout, fulladder_9_s);
endmodule
